// Logisim project labo_alu_etu.circ as structural Verilog: 10 circuits, main circuit ALU_MAXV
module ALU_MAXV (
  input  [3:0] a_i,
  input  [3:0] b_i,
  output erreur_o,
  output [3:0] c_o
);

  wire [5:0] opcode_i_sw6;

  DipSwitch opcode_i (
    .sw1(opcode_i_sw6[5]), .sw2(opcode_i_sw6[4]), .sw3(opcode_i_sw6[3]), .sw4(opcode_i_sw6[2]),
    .sw5(opcode_i_sw6[1]), .sw6(opcode_i_sw6[0]));  // open: sw7, sw8
  ALU_Top alu_inst (.a_i(a_i), .b_i(b_i), .op_i(opcode_i_sw6), .erreur_o(erreur_o), .c_o(c_o));

  // Notes on the sheet:
  //   Attention, votre version de Logisim
  //   ne contient pas de tracker. Si vous
  //   enregistrez votre projet, toutes les
  //   informations du tracker seront
  //   définitivement effacées.
endmodule

module ALU_Top (
  input  [3:0] a_i,
  input  [3:0] b_i,
  input  [5:0] op_i,
  output erreur_o,
  output [3:0] c_o
);

  wire AddSubALU_1_carry_o, AddSubALU_1_negative_o, AddSubALU_1_overflow_o, AddSubALU_1_zero_o, and_1_out,
       and_2_out, and_3_out;
  wire [3:0] AddSubALU_1_r_o, ComparateurALU_1_cmp_o, CustomALU_1_s_o, UniteLogiqueALU_1_f_o;

  AddSubALU AddSubALU_1 (
    .a_i(a_i), .b_i(b_i), .op_i(op_i[3:2]), .overflow_o(AddSubALU_1_overflow_o), .Zero_o(AddSubALU_1_zero_o),
    .r_o(AddSubALU_1_r_o), .carry_o(AddSubALU_1_carry_o), .Negative_o(AddSubALU_1_negative_o));
  ComparateurALU ComparateurALU_1 (
    .a(a_i), .b(b_i), .Negative_i(AddSubALU_1_negative_o), .op_i(op_i[2:0]), .zero_i(AddSubALU_1_zero_o),
    .carry_i(AddSubALU_1_carry_o), .cmp_o(ComparateurALU_1_cmp_o));
  UniteLogiqueALU UniteLogiqueALU_1 (.a_i(a_i), .b_i(b_i), .op_i(op_i[1:0]), .f_o(UniteLogiqueALU_1_f_o));
  CustomALU CustomALU_1 (.a_i(a_i), .s_o(CustomALU_1_s_o));
  and and_1 (and_1_out, ~op_i[3], op_i[4], ~op_i[5]);  // AND_Gate
  and and_2 (and_2_out, ~op_i[4], ~op_i[5]);  // AND_Gate
  and and_3 (and_3_out, and_2_out, AddSubALU_1_overflow_o);
  or or_1 (erreur_o, and_3_out, and_1_out);
  SelectorALU SelectorALU_1 (
    .AddSub_i(AddSubALU_1_r_o), .Comparateur_i(ComparateurALU_1_cmp_o),
    .UniteLogique_i(UniteLogiqueALU_1_f_o), .Cusom_i(CustomALU_1_s_o), .op_i(op_i), .r_o(c_o));

  // Notes on the sheet:
  //   Attention, votre version de Logisim
  //   ne contient pas de tracker. Si vous
  //   enregistrez votre projet, toutes les
  //   informations du tracker seront
  //   définitivement effacées.
endmodule

module Add1Bit (
  input  a_i,
  input  b_i,
  input  c_i,
  output r_o,
  output c_o
);

  wire and_1_out, and_2_out, and_3_out, xor_1_out;

  xor xor_1 (xor_1_out, a_i, b_i);
  and and_1 (and_1_out, a_i, b_i);
  and and_2 (and_2_out, a_i, c_i);
  and and_3 (and_3_out, b_i, c_i);
  xor xor_2 (r_o, xor_1_out, c_i);
  or or_1 (c_o, and_1_out, and_2_out, and_3_out);

  // Notes on the sheet:
  //   Attention, votre version de Logisim
  //   ne contient pas de tracker. Si vous
  //   enregistrez votre projet, toutes les
  //   informations du tracker seront
  //   définitivement effacées.
endmodule

module Add4Bit (
  input  c_i,
  input  [3:0] a_i,
  input  [3:0] b_i,
  output [3:0] r_o,
  output c_o
);

  wire c_i1, c_i2, c_i3;

  Add1Bit Add1Bit_1 (.a_i(a_i[0]), .b_i(b_i[0]), .c_i(c_i), .r_o(r_o[0]), .c_o(c_i1));
  Add1Bit Add1Bit_2 (.a_i(a_i[1]), .b_i(b_i[1]), .c_i(c_i1), .r_o(r_o[1]), .c_o(c_i2));
  Add1Bit Add1Bit_3 (.a_i(a_i[2]), .b_i(b_i[2]), .c_i(c_i2), .r_o(r_o[2]), .c_o(c_i3));
  Add1Bit Add1Bit_4 (.a_i(a_i[3]), .b_i(b_i[3]), .c_i(c_i3), .r_o(r_o[3]), .c_o(c_o));

  // Notes on the sheet:
  //   Attention, votre version de Logisim
  //   ne contient pas de tracker. Si vous
  //   enregistrez votre projet, toutes les
  //   informations du tracker seront
  //   définitivement effacées.
endmodule

module AddSub4Bit (
  input  [3:0] a_i,
  input  sel_i,
  input  [3:0] b_i,
  output [3:0] r_o,
  output c_o
);

  wire [3:0] xor_1_out;

  assign xor_1_out = {4{sel_i}} ^ b_i;  // XOR_Gate xor_1, 4 bits wide
  Add4Bit Add4Bit_1 (.c_i(sel_i), .a_i(a_i), .b_i(xor_1_out), .r_o(r_o), .c_o(c_o));

  // Notes on the sheet:
  //   Attention, votre version de Logisim
  //   ne contient pas de tracker. Si vous
  //   enregistrez votre projet, toutes les
  //   informations du tracker seront
  //   définitivement effacées.
endmodule

module AddSubALU (
  input  [3:0] a_i,
  input  [3:0] b_i,
  input  [1:0] op_i,
  output overflow_o,
  output Zero_o,
  output [3:0] r_o,
  output carry_o,
  output Negative_o
);

  wire and_2_out, and_3_out, and_4_out, and_5_out, and_6_out, and_7_out;

  AddSub4Bit l (.a_i(a_i), .sel_i(op_i[1]), .b_i(b_i), .r_o(r_o), .c_o(carry_o));
  and and_1 (Negative_o, r_o[3], op_i[1]);
  nor nor_1 (Zero_o, r_o[0], r_o[1], r_o[2], r_o[3]);
  and and_2 (and_2_out, ~op_i[0], a_i[3], ~b_i[3], op_i[1], ~r_o[3]);  // AND_Gate
  and and_3 (and_3_out, ~op_i[0], ~a_i[3], b_i[3], op_i[1], r_o[3]);  // AND_Gate
  and and_4 (and_4_out, ~op_i[0], a_i[3], b_i[3], ~op_i[1], ~r_o[3]);  // AND_Gate
  and and_5 (and_5_out, ~op_i[0], ~a_i[3], ~b_i[3], ~op_i[1], r_o[3]);  // AND_Gate
  and and_6 (and_6_out, ~carry_o, op_i[1], op_i[0]);  // AND_Gate
  and and_7 (and_7_out, carry_o, ~op_i[1], op_i[0]);  // AND_Gate
  or or_1 (overflow_o, and_2_out, and_3_out, and_4_out, and_5_out, and_6_out, and_7_out);

  // Notes on the sheet:
  //   Attention, votre version de Logisim
  //   ne contient pas de tracker. Si vous
  //   enregistrez votre projet, toutes les
  //   informations du tracker seront
  //   définitivement effacées.
endmodule

module ComparateurALU (
  input  [3:0] a,
  input  [3:0] b,
  input  Negative_i,
  input  [2:0] op_i,
  input  zero_i,
  input  carry_i,
  output [3:0] cmp_o
);

  wire and_1_out, and_2_out, and_3_out, and_4_out, and_5_out, not_1_out, not_2_out, or_1_out;

  and and_1 (and_1_out, a[3], ~b[3]);  // AND_Gate
  and and_2 (and_2_out, a[3], ~b[3]);  // AND_Gate
  and and_3 (and_3_out, ~b[3], ~a[3], Negative_i);  // AND_Gate
  and and_4 (and_4_out, and_2_out, Negative_i);
  or or_1 (or_1_out, and_1_out, and_3_out, and_4_out);
  and and_5 (and_5_out, ~a[3], b[3], ~Negative_i);  // AND_Gate
  not not_1 (not_1_out, zero_i);
  not not_2 (not_2_out, carry_i);
  Multiplexer #(.select(3), .enable("false")) multiplexer_1 (
    .in0(1'b0), .in1(and_5_out), .in2(or_1_out), .in3(not_1_out), .in4(zero_i), .in5(carry_i),
    .in6(not_2_out), .in7(1'b0), .out(cmp_o[0]), .sel(op_i));

  assign cmp_o[3:1] = 3'b000;

  // Notes on the sheet:
  //   Attention, votre version de Logisim
  //   ne contient pas de tracker. Si vous
  //   enregistrez votre projet, toutes les
  //   informations du tracker seront
  //   définitivement effacées.
endmodule

module UniteLogiqueALU (
  input  [3:0] a_i,
  input  [3:0] b_i,
  input  [1:0] op_i,
  output [3:0] f_o
);

  wire [3:0] NonSigne_1_out, NonSigne_2_out, Signe_1_out, Signe_2_out;

  assign Signe_1_out = a_i & b_i;  // AND_Gate Signe_1, 4 bits wide
  assign Signe_2_out = a_i | b_i;  // OR_Gate Signe_2, 4 bits wide
  assign NonSigne_1_out = ~(a_i & b_i);  // NAND_Gate NonSigne_1, 4 bits wide
  assign NonSigne_2_out = a_i ^ b_i;  // XOR_Gate NonSigne_2, 4 bits wide
  Multiplexer #(.select(2), .width(4), .enable("false")) multiplexer_1 (
    .in0(Signe_1_out), .in1(Signe_2_out), .in2(NonSigne_1_out), .in3(NonSigne_2_out), .out(f_o), .sel(op_i));

  // Notes on the sheet:
  //   Attention, votre version de Logisim
  //   ne contient pas de tracker. Si vous
  //   enregistrez votre projet, toutes les
  //   informations du tracker seront
  //   définitivement effacées.
endmodule

module CustomALU (
  input  [3:0] a_i,
  output [3:0] s_o
);

  wire [1:0] Add1Bit_1_r_o, Add1Bit_2_r_o;

  Add1Bit Add1Bit_2 (.a_i(a_i[2]), .b_i(a_i[3]), .r_o(Add1Bit_2_r_o[0]), .c_o(Add1Bit_2_r_o[1]));  // open: c_i
  Add1Bit Add1Bit_1 (.a_i(a_i[0]), .b_i(a_i[1]), .r_o(Add1Bit_1_r_o[0]), .c_o(Add1Bit_1_r_o[1]));  // open: c_i
  Add4Bit Add4Bit_1 (.a_i({2'b00, Add1Bit_1_r_o}), .b_i({2'b00, Add1Bit_2_r_o}), .r_o(s_o));  // open: c_i, c_o

  // Notes on the sheet:
  //   Attention, votre version de Logisim
  //   ne contient pas de tracker. Si vous
  //   enregistrez votre projet, toutes les
  //   informations du tracker seront
  //   définitivement effacées.
endmodule

module SelectorALU (
  input  [3:0] AddSub_i,
  input  [3:0] Comparateur_i,
  input  [3:0] UniteLogique_i,
  input  [3:0] Cusom_i,
  input  [5:0] op_i,
  output [3:0] r_o
);

  Multiplexer #(.select(2), .width(4), .enable("false")) multiplexer_1 (
    .in0(AddSub_i), .in1(Comparateur_i), .in2(UniteLogique_i), .in3(Cusom_i), .out(r_o), .sel(op_i[5:4]));

  // Notes on the sheet:
  //   Attention, votre version de Logisim
  //   ne contient pas de tracker. Si vous
  //   enregistrez votre projet, toutes les
  //   informations du tracker seront
  //   définitivement effacées.
endmodule
