// Logisim project labo_chenillard_etu.circ as structural Verilog: 5 circuits, main circuit MAXV_CHENILLARD
module MAXV_CHENILLARD (
  input  load_i,
  input  [7:0] switch_i,
  input  clk_i,
  input  nReset_i,
  output [7:0] led_o
);

  wire entree_i_sw7, entree_i_sw8, not_1_out;
  wire [1:0] entree_i_sw2;

  DipSwitch entree_i (
    .sw1(entree_i_sw2[1]), .sw2(entree_i_sw2[0]), .sw7(entree_i_sw7), .sw8(entree_i_sw8));  // open: sw3, sw4, sw5, sw6
  not not_1 (not_1_out, nReset_i);
  chenillard_TOP chenillard_top_1 (
    .load_i(load_i), .enable_i(entree_i_sw7), .right_nleft_i(entree_i_sw8), .speed_i(entree_i_sw2),
    .val_i(switch_i), .clk_i(clk_i), .reset_i(not_1_out), .led_o(led_o));

  // Notes on the sheet:
  //   Attention, votre version de Logisim
  //   ne contient pas de tracker. Si vous
  //   enregistrez votre projet, toutes les
  //   informations du tracker seront
  //   définitivement effacées.
endmodule

module chenillard_TOP (
  input  load_i,
  input  enable_i,
  input  right_nleft_i,
  input  [1:0] speed_i,
  input  [7:0] val_i,
  input  clk_i,
  input  reset_i,
  output [7:0] led_o
);


  // Notes on the sheet:
  //   Attention, votre version de Logisim
  //   ne contient pas de tracker. Si vous
  //   enregistrez votre projet, toutes les
  //   informations du tracker seront
  //   définitivement effacées.
endmodule

module shift_reg_4b (
  input  [1:0] mode_i,
  input  clk_i,
  input  reset_i,
  input  ser_l_i,
  input  ser_r_i,
  input  [3:0] value_load_i,
  output [3:0] val_o
);

  wire multiplexer_2_out, multiplexer_3_out, multiplexer_4_out, multiplexer_5_out;
  wire [3:0] multiplexer_1_out;

  Multiplexer #(.select(2), .width(4), .enable("false")) multiplexer_1 (
    .in0(4'b0000), .in1(value_load_i), .in2(4'b0000), .in3(4'b0000), .out(multiplexer_1_out), .sel(mode_i));
  Multiplexer #(.select(2), .enable("false")) multiplexer_2 (
    .in0(val_o[3]), .in1(multiplexer_1_out[3]), .in2(val_o[2]), .in3(ser_r_i), .out(multiplexer_2_out),
    .sel(mode_i));
  D_Flip_Flop d_ff_1 (.D(multiplexer_2_out), .clk(clk_i), .Q(val_o[3]), .reset(reset_i));  // open: Qn, preset
  D_Flip_Flop d_ff_2 (.D(multiplexer_3_out), .clk(clk_i), .Q(val_o[2]), .reset(reset_i));  // open: Qn, preset
  Multiplexer #(.select(2), .enable("false")) multiplexer_3 (
    .in0(val_o[2]), .in1(multiplexer_1_out[2]), .in2(val_o[1]), .in3(val_o[3]), .out(multiplexer_3_out),
    .sel(mode_i));
  D_Flip_Flop d_ff_3 (.D(multiplexer_4_out), .clk(clk_i), .Q(val_o[1]), .reset(reset_i));  // open: Qn, preset
  Multiplexer #(.select(2), .enable("false")) multiplexer_4 (
    .in0(val_o[1]), .in1(multiplexer_1_out[1]), .in2(val_o[0]), .in3(val_o[2]), .out(multiplexer_4_out),
    .sel(mode_i));
  Multiplexer #(.select(2), .enable("false")) multiplexer_5 (
    .in0(val_o[0]), .in1(multiplexer_1_out[0]), .in2(ser_l_i), .in3(val_o[1]), .out(multiplexer_5_out),
    .sel(mode_i));
  D_Flip_Flop d_ff_4 (.D(multiplexer_5_out), .clk(clk_i), .Q(val_o[0]), .reset(reset_i));  // open: Qn, preset

  // Other names for the same wires on the sheet: Clock = clk_i; Mode[1:0] = mode_i; Reset = reset_i

  // Notes on the sheet:
  //   Attention, votre version de Logisim
  //   ne contient pas de tracker. Si vous
  //   enregistrez votre projet, toutes les
  //   informations du tracker seront
  //   définitivement effacées.
endmodule

module shift_reg_8b (
  input  [1:0] mode_i,
  input  clk_i,
  input  reset_i,
  input  ser_r_i,
  input  ser_l_i,
  input  [7:0] value_load_i,
  output [7:0] val_o
);

  shift_reg_4b shift_reg_4b_1 (
    .mode_i(mode_i), .clk_i(clk_i), .reset_i(reset_i), .ser_l_i(ser_l_i), .ser_r_i(ser_r_i),
    .value_load_i(value_load_i[3:0]), .val_o(val_o[3:0]));
  shift_reg_4b shift_reg_4b_2 (
    .mode_i(mode_i), .clk_i(clk_i), .reset_i(reset_i), .ser_l_i(ser_l_i), .ser_r_i(ser_r_i),
    .value_load_i(value_load_i[7:4]), .val_o(val_o[7:4]));

  // Other names for the same wires on the sheet: Clock = clk_i; Left = ser_l_i; Mode[1:0] = mode_i; Reset = reset_i;
  //   Right = ser_r_i

  // Notes on the sheet:
  //   Attention, votre version de Logisim
  //   ne contient pas de tracker. Si vous
  //   enregistrez votre projet, toutes les
  //   informations du tracker seront
  //   définitivement effacées.
endmodule

module timer_28b (
  input  [27:0] value_i,
  input  en_i,
  input  load_i,
  input  clk_i,
  input  reset_i,
  output done_o
);


  // Notes on the sheet:
  //   Attention, votre version de Logisim
  //   ne contient pas de tracker. Si vous
  //   enregistrez votre projet, toutes les
  //   informations du tracker seront
  //   définitivement effacées.
endmodule
